# Fritzing sketch ATmelProgrammer (saved by Fritzing 0.9.3b)
circuit board: 7.27279cm x 6.49016cm
breadboards: 1

parts:
  ZIF_SOCKET1 = Aries 28-6574-10 28W ZIF Socket [part_number=28-6574-10]
  XTAL1 = Crystal [frequency="16 Mhz" package=THT]
  Arduino_Nano = Arduino Nano (Rev3.0)
  C1 = Ceramic Capacitor [capacitance=22pF package="100 mil [THT, multilayer]"]
  C3 = Ceramic Capacitor [capacitance=22pF package="100 mil [THT, multilayer]"]
  J1 = male pin header, 2 pins [form="♂ (male)"]
  J2 = male pin header, 2 pins [form="♂ (male)"]
  J3 = male pin header, 2 pins [form="♂ (male)"]
  J4 = male pin header, 2 pins [form="♂ (male)"]
  J5 = male pin header, 2 pins [form="♂ (male)"]
  J6 = male pin header, 2 pins [form="♂ (male)"]
  J7 = male pin header, 2 pins [form="♂ (male)"]

nets:
  N1: ZIF_SOCKET1.Pin_1, Arduino_Nano.D10
  N2: ZIF_SOCKET1.Pin_4, J5.pin1
  N3: ZIF_SOCKET1.Pin_7, Arduino_Nano.5V, J1.pin1
  N4: ZIF_SOCKET1.Pin_8, Arduino_Nano.GND, C1.1, C3.0, J5.pin2
  N5: ZIF_SOCKET1.Pin_9, XTAL1.pin_0, C1.0
  N6: ZIF_SOCKET1.Pin_10, XTAL1.pin_1, C3.1
  N7: ZIF_SOCKET1.Pin_17, Arduino_Nano.D11/MOSI, J4.pin2
  N8: ZIF_SOCKET1.Pin_18, Arduino_Nano.D12/MISO, J3.pin2
  N9: ZIF_SOCKET1.Pin_19, Arduino_Nano.D13/SCK, J2.pin2
  N10: ZIF_SOCKET1.Pin_23, J2.pin1, J6.pin1
  N11: ZIF_SOCKET1.Pin_24, J3.pin1, J7.pin1
  N12: ZIF_SOCKET1.Pin_25, J4.pin1
  N13: ZIF_SOCKET1.Pin_26, J7.pin2
  N14: ZIF_SOCKET1.Pin_27, J6.pin2
  N15: ZIF_SOCKET1.Pin_28, J1.pin2

notes:
  J1-7 open   : ATMega328
  J1-7 closed : ATtiny85
