# Fritzing sketch SerialToPCD8544 (saved by Fritzing 0.9.3b)
circuit board: 2.05069cm x 2.52914cm
breadboards: 1

parts:
  J1 = female pin header, 8 pins [form="♀ (female)"]
  G_V_S = female pin header, 3 pins [form="♀ (female)"]
  U1 = attiny85 [package=dip]
  10K = Resistor [tolerance=±5% resistance=10k package=THT]

nets:
  N1: J1.pin1, J1.pin7, G_V_S.pin1, U1.Pin_4
  N2: J1.pin3, G_V_S.pin2, U1.Pin_8, 10K.Pin_1
  N3: J1.pin4, U1.Pin_6
  N4: J1.pin5, U1.Pin_7
  N5: J1.pin6, U1.Pin_2
  N6: J1.pin8, U1.Pin_3
  N7: G_V_S.pin3, U1.Pin_5
  N8: U1.Pin_1, 10K.Pin_0

notes:
  RST
  CE
  DC
  DIN
  CLK
  VCC
  BL
  GND
