# Fritzing sketch SmartCarController (saved by Fritzing 0.9.3b)
circuit board: 7.26413cm x 4.41113cm

parts:
  ATTiny85 = attiny85 [package=dip]
  R1 = Resistor [tolerance=±5% resistance=10k package=THT]
  XTAL1 = Crystal [frequency="16 Mhz" package=THT]
  C1 = Ceramic Capacitor [capacitance=22pF package="200 mil [THT, multilayer]"]
  C2 = Ceramic Capacitor [capacitance=22pF package="200 mil [THT, multilayer]"]
  ULN_2003 = ULN2003A [package="DIP16 [THT]"]
  J5 = female pin header, 7 pins [form="♀ (female)"]
  J4 = female pin header, 7 pins [form="♀ (female)"]
  J3 = female pin header, 5 pins [form="♀ (female)"]
  J1 = female pin header, 6 pins [form="♀ (female)"]
  J7 = female pin header, 2 pins [form="♀ (female)"]
  J6 = female pin header, 2 pins [form="♀ (female)"]
  R2 = Resistor [tolerance=±5% resistance=10k package=THT]
  C3 = Ceramic Capacitor [capacitance=100nF package="100 mil [THT, multilayer]"]
  C4 = Electrolytic Capacitor [capacitance=10µF package="100 mil [THT, electrolytic]"]
  J2 = female pin header, 3 pins [form="♀ (female)"]
  R3 = Resistor [tolerance=±5% resistance=1k package=THT]
  L1 = LED - 5mm [color="Blue (525nm)" package="5 mm [THT]"]
  L2 = LED - 5mm [color="Green (570nm)" package="5 mm [THT]"]
  R4 = Resistor [tolerance=±5% resistance=1k package=THT]
  ATMega328PU = atmega328 [package=dip]
  J8 = female pin header, 6 pins [form="♀ (female)"]
  J9 = female pin header, 6 pins [form="♀ (female)"]
  J10 = female pin header, 6 pins [form="♀ (female)"]

nets:
  N1: ATTiny85.Pin_1, R2.Pin_1
  N2: ATTiny85.Pin_2, ULN_2003.In_7
  N3: ATTiny85.Pin_3, ULN_2003.In_6
  N4: ATTiny85.Pin_4, C1.0, C2.1, C3.0, ATMega328PU.GND#7, J8.pin1, J8.pin2, J8.pin3, J8.pin4, J8.pin5, J8.pin6
  N5: ATTiny85.Pin_5, ATMega328PU.D8
  N6: ATTiny85.Pin_6, J6.pin1
  N7: ATTiny85.Pin_7, J6.pin2
  N8: ATTiny85.Pin_8, R1.Pin_0, R2.Pin_0, C3.1, C4.+, J2.pin1, R4.Pin_0, ATMega328PU.VCC, ATMega328PU.AVCC, ATMega328PU.AREF, J9.pin1, J9.pin2, J9.pin3, J9.pin4, J9.pin5, J9.pin6
  N9: R1.Pin_1, ATMega328PU.RESET
  N10: XTAL1.pin_0, C2.0, ATMega328PU.XLAT1
  N11: XTAL1.pin_1, C1.1, ATMega328PU.XLAT2
  N12: ULN_2003.In_1, J3.pin2, ATMega328PU.D12
  N13: ULN_2003.In_2, J3.pin1, R3.Pin_1, ATMega328PU.D13
  N14: ULN_2003.In_3, J3.pin3, ATMega328PU.D11_(PWM)
  N15: ULN_2003.In_4, J3.pin4, ATMega328PU.D10_(PWM)
  N16: ULN_2003.In_5, J3.pin5, ATMega328PU.D9_(PWM)
  N17: ULN_2003.0V, C4.-, J2.pin2, L1.cathode, L2.cathode, ATMega328PU.GND#21
  N18: ULN_2003.COM_-_Common, J5.pin1, J5.pin2, J5.pin3, J5.pin4, J5.pin5, J5.pin6, J5.pin7, J2.pin3
  N19: ULN_2003.Out_7, J4.pin7
  N20: ULN_2003.Out_6, J4.pin6
  N21: ULN_2003.Out_5, J4.pin5
  N22: ULN_2003.Out_4, J4.pin4
  N23: ULN_2003.Out_3, J4.pin3
  N24: ULN_2003.Out_2, J4.pin2
  N25: ULN_2003.Out_1, J4.pin1
  N26: J1.pin1, ATMega328PU.A5
  N27: J1.pin2, ATMega328PU.A4
  N28: J1.pin3, ATMega328PU.A3
  N29: J1.pin4, ATMega328PU.A2
  N30: J1.pin5, ATMega328PU.A1
  N31: J1.pin6, ATMega328PU.A0
  N32: J7.pin1, ATMega328PU.D1_(TX)
  N33: J7.pin2, ATMega328PU.D0_(RX)
  N34: R3.Pin_0, L1.anode
  N35: L2.anode, R4.Pin_1
  N36: ATMega328PU.D2, J10.pin4
  N37: ATMega328PU.D3_(PWM), J10.pin5
  N38: ATMega328PU.D4, J10.pin6
  N39: ATMega328PU.D5_(PWM), J10.pin1
  N40: ATMega328PU.D6_(PWM), J10.pin2
  N41: ATMega328PU.D7, J10.pin3

notes:
  right wheel pwm out
  left wheel pwm out
  right wheel speed encoder IN
  serial cmd in
  +5V Gnd Gnd +12V
  left wheel speed encoder IN
  right wheel 0v
  left wheel 0v
  right wheel +12v
  left wheel +12v
  digital out 0-4 0v
  digital out 0-4 +12v
  S/R
  S/L
  PWM3
  PWM4
  PWM5
  PWM0
  PWM1
  PWM2
  R
  L
  M0
  M1
  M2
  M3
  M4
  +12V
  Gnd
  +5V
  A0
  A1
  A2
  A3
  A4
  A5
  RX
  TX
  D0
  D1
  D2
  D3
  D4
  link
  XTAL1=16Mhz
  C1=C2=22pF
  R1=R2=10KOhm
  J1 A in
  J2 Power
  J3 D out
  J4 Gnd
  J5 +12v
  J6 speed in
  J7 serial
  J8 Gnd
  J9 +5v
  J10 PWM
  C3=100nF
  C4=10uF
  R3=R4=1KOhm
  L1=L2=led
  SMC V1.1
  (c) B.A.T. Cave
