# Fritzing sketch SmartCarControllerHat-smt (saved by Fritzing 0.9.3b)
circuit board: 6.52336cm x 4.33832cm

parts:
  J4 = female pin header, 6 pins [form="♀ (female)"]
  J5 = female pin header, 6 pins [form="♀ (female)"]
  J6 = female pin header, 6 pins [form="♀ (female)"]
  J9 = double row female pin header, 6 pins [form="♀ (female)"]
  RPi = Raspberry Pi 3 [part_number=RPI-3-V1.2]
  IC6 = SO14 [chip_label=ATTiny24/44/84 package=SO]
  J10 = double row female pin header, 8 pins [form="♀ (female)"]
  U1 = ATmega328 [package=tqfp]
  Composant2 = SO08 [chip_label=L293DD-TOP package=SO]
  Composant3 = SO08 [chip_label=L293DD-BOTTOM package=SO]
  J11 = female pin header, 3 pins [form="♀ (female)"]
  R1 = Resistor [tolerance=±5% resistance=10k package="0805 [SMD]"]
  Y4 = Resonator [part_number="CSTCE 16M0V53" package=resonator-smd]
  R2 = Resistor [tolerance=±5% resistance=10k package="0805 [SMD]"]
  J12 = female pin header, 3 pins [form="♀ (female)"]
  J13 = female pin header, 3 pins [form="♀ (female)"]

nets:
  N1: J4.pin1, J4.pin2, J4.pin3, J4.pin4, J4.pin5, J4.pin6, J9.pin2, J9.pin5, J11.pin2
  GND: J5.pin1, J5.pin2, J5.pin3, J5.pin4, J5.pin5, J5.pin6, J9.pin3, J9.pin4, RPi.GND, IC6.14, J10.pin1, J10.pin2, J10.pin3, J10.pin4, U1.GND, U1.AGND, Composant2.4, Composant3.1, J11.pin3, Y4.2
  N2: J6.pin1, U1.PD2(INT0)
  N3: J6.pin2, U1.PD3(INT1)
  N4: J6.pin3, U1.PD4(XCK_T0)
  N5: J6.pin4, U1.PD5(T1)
  N6: J6.pin5, U1.PD6(AIN0)
  N7: J6.pin6, U1.PD7(AIN1)
  N8: J9.pin1, IC6.2
  N9: J9.pin6, IC6.3
  N10: RPi.GPIO17, IC6.8
  N11: RPi.GPIO10, IC6.9
  N12: RPi.GPIO9, IC6.7
  N13: RPi.GPIO11, IC6.4, R1.Pin_1
  N14: RPi.ID_SD, U1.PB5(SCK)
  N15: RPi.GPIO5, U1.PB4(MISO)
  N16: RPi.GPIO6, U1.PB3(MOSI_OC2)
  N17: RPi.GPIO21, U1.PC6(_RESET), R2.Pin_0
  N18: RPi.GPIO15, U1.PD1(TXD)
  N19: RPi.GPIO14, U1.PD0(RXD)
  5V: RPi.5V, IC6.1, U1.VCC, U1.AVCC, Composant2.1, Composant2.8, Composant3.5, R1.Pin_0, R2.Pin_1
  N20: IC6.5, U1.PB0(ICP)
  N21: IC6.10, Composant2.7
  N22: IC6.11, Composant3.6
  N23: IC6.12, Composant3.3
  N24: IC6.13, Composant2.2
  N25: J10.pin5, Composant3.2
  N26: J10.pin6, Composant2.3
  N27: J10.pin7, Composant2.6
  N28: J10.pin8, Composant3.7
  N29: U1.PB6(XTAL1_TOSC1), Y4.1
  N30: U1.PB7(XTAL2_TOSC2), Y4.3
  N31: U1.PC0(ADC0), J13.pin3
  N32: U1.PC1(ADC1), J13.pin2
  N33: U1.PC2(ADC2), J13.pin1
  N34: U1.PC3(ADC3), J12.pin1
  N35: U1.PC4(ADC4_SDA), J12.pin2
  N36: U1.PC5(ADC5_SCL), J12.pin3
  N37: Composant2.5, Composant3.8
  N38: Composant3.4, J11.pin1

notes:
  right wheel pwm out
  left wheel pwm out
  right wheel speed encoder IN
  serial cmd in
  +5V Gnd Gnd +12V
  left wheel speed encoder IN
  right wheel 0v
  left wheel 0v
  right wheel +12v
  left wheel +12v
  digital out 0-4 0v
  digital out 0-4 +12v
  GND
  +5v
  +12v
