# Fritzing sketch lcd1602 (saved by Fritzing 0.9.3b)
circuit board: 6.76497cm x 5.00909cm
breadboards: 1

parts:
  LCD1 = LCD screen [part_number=QY-1602A]
  J1 = female pin header, 10 pins [form="♀ (female)"]
  R1 = Rotary Potentiometer (Large) [maximum_resistance=100kΩ package=THT]
  Composant2 = Arduino Nano (Rev3.0)

nets:
  VSS: LCD1.VSS, LCD1.R/W, LCD1.LED-, J1.pin2, R1.leg1, Composant2.GND
  VDD: LCD1.VDD, LCD1.LED+, J1.pin4, R1.leg2, Composant2.5V
  N1: LCD1.V0, R1.wiper
  N2: LCD1.RS, Composant2.D2
  N3: LCD1.E, Composant2.D3
  N4: LCD1.DB4, Composant2.D4
  N5: LCD1.DB5, Composant2.D5
  N6: LCD1.DB6, Composant2.D6
  N7: LCD1.DB7, Composant2.D7
  N8: J1.pin1, Composant2.VIN
  N9: J1.pin3, Composant2.RESET
  N10: J1.pin5, Composant2.D13/SCK
  N11: J1.pin6, Composant2.D1/TX
  N12: J1.pin7, Composant2.D0/RX
  N13: J1.pin8, Composant2.D10
  N14: J1.pin9, Composant2.D11/MOSI
  N15: J1.pin10, Composant2.D12/MISO
